// Digital circuit CPU.dig as structural Verilog
module CPU (
  input  CLOCK
);

  wire alu_8_bit_1_zero, and_1_out;
  wire [2:0] Instruction_Memory_d_2, Instruction_Memory_d_3, multiplexer_1_out;
  wire [5:0] Instruction_Memory_d;
  wire [7:0] add_1_s, add_2_s, alu_8_bit_1_s, barrelshifter_1_out, bitextender_1_out, Data_Memory_d,
       multiplexer_2_out, multiplexer_3_out, multiplexer_4_out, multiplexer_5_out, PC_q, Registers_da,
       Registers_db;
  wire [15:12] Instruction_Memory_d_4;

  Register #(.Bits(8), .isProgramCounter("true")) PC (.D(multiplexer_3_out), .C(CLOCK), .en(CLOCK), .Q(PC_q));
  Add #(.Bits(8)) add_1 (.a(8'h4), .b(PC_q), .c_i(1'b0), .s(add_1_s));  // open: c_o
  ROM #(.AddrBits(8), .isProgramMemory("true"), .Bits(16)) Instruction_Memory (
    .A(PC_q), .sel(1'b1),
    .D({Instruction_Memory_d_4, Instruction_Memory_d_3, Instruction_Memory_d_2, Instruction_Memory_d}));
  Multiplexer #(.Bits(3)) multiplexer_1 (
    .in_0(Instruction_Memory_d[5:3]), .in_1(Instruction_Memory_d_2), .out(multiplexer_1_out));  // open: sel
  BitExtender #(.inputBits(6), .outputBits(8)) bitextender_1 (.in(Instruction_Memory_d), .out(bitextender_1_out));
  BarrelShifter #(.Bits(8)) barrelshifter_1 (.in(bitextender_1_out), .shift(8'h2), .out(barrelshifter_1_out));
  Add #(.Bits(8)) add_2 (.a(add_1_s), .b(barrelshifter_1_out), .s(add_2_s));  // open: c_i, c_o
  Multiplexer #(.Bits(8)) multiplexer_2 (.sel(and_1_out), .in_0(add_1_s), .in_1(add_2_s), .out(multiplexer_2_out));
  Multiplexer #(.Bits(8)) multiplexer_3 (
    .in_0(multiplexer_2_out), .in_1({Instruction_Memory_d_2[1:0], Instruction_Memory_d}),
    .out(multiplexer_3_out));  // open: sel
  RegisterFile #(.AddrBits(3), .Bits(8)) Registers (
    .Din(multiplexer_5_out), .Rw(multiplexer_1_out), .C(CLOCK), .Ra(Instruction_Memory_d_3),
    .Rb(Instruction_Memory_d_2), .Da(Registers_da), .Db(Registers_db));  // open: we
  buf and_1 (and_1_out, alu_8_bit_1_zero);  // And open: In_2
  Multiplexer #(.Bits(8)) multiplexer_4 (
    .in_0(Registers_db), .in_1(bitextender_1_out), .out(multiplexer_4_out));  // open: sel
  ALU_8_BIT alu_8_bit_1 (
    .ZERO(alu_8_bit_1_zero), .S(alu_8_bit_1_s), .A(Registers_da), .B(multiplexer_4_out));  // open: ALUop, HIGH, SHAMT
  RAMDualPort #(.AddrBits(8), .Bits(8)) Data_Memory (
    .A(alu_8_bit_1_s), .Din(Registers_db), .C(CLOCK), .D(Data_Memory_d));  // open: str, ld
  Multiplexer #(.Bits(8)) multiplexer_5 (
    .in_0(Data_Memory_d), .in_1(alu_8_bit_1_s), .out(multiplexer_5_out));  // open: sel

  // Notes on the sheet:
  //   contents of Instruction_Memory (hex, n*v repeats v):
  //   0,21
  //   ADDR
  //   OPCODE
  //   Only Use 8 bits of Address
  //   IMM
  //   RT
  //   RS
  //   FUNCT
  //   RD
  //   RegDst
  //   Jump
  //   Branch
  //   ALUSrc
  //   MemtoReg
endmodule
